// Logisim project Logisim tp3.circ as structural Verilog: 1 circuit, main circuit main
module main (
  input  in_1,
  input  in_2,
  input  in_3,
  input  in_4,
  input  in_5,
  input  in_6,
  input  in_7,
  input  in_8,
  input  in_9,
  input  in_10,
  input  in_11,
  input  in_12,
  input  in_13,
  input  in_14,
  input  in_15,
  input  in_16,
  input  in_17,
  input  in_18,
  input  in_19,
  output out_20,
  output out_21,
  output out_22,
  output out_23,
  output out_24,
  output out_25,
  output out_26,
  output out_27,
  output out_28,
  output out_29,
  output out_30,
  output out_31
);

  wire adder_1_cout, adder_2_cout, adder_3_cout, and_1_out, and_2_out, xor_1_out;

  xor xor_1 (xor_1_out, in_1, in_2);
  and and_1 (and_1_out, in_1, in_2);
  xor xor_2 (out_20, xor_1_out, in_3);
  and and_2 (and_2_out, xor_1_out, in_3);
  _74283 #(.ShowInternalStructure("true")) u_74283_1 (
    .pin1(out_25), .pin2(in_10), .pin3(in_6), .pin4(out_26), .pin5(in_7), .pin6(in_11), .pin15(in_9),
    .pin14(in_5), .pin13(out_24), .pin12(in_8), .pin11(in_4), .pin10(out_23), .pin9(out_22));  // open: pin7
  or or_1 (out_21, and_2_out, and_1_out);
  Adder #(.width(1)) adder_1 (.a(in_15), .b(in_19), .out(out_31), .cin(1'b0), .cout(adder_1_cout));
  Adder #(.width(1)) adder_2 (.a(in_14), .b(in_18), .out(out_30), .cin(adder_1_cout), .cout(adder_2_cout));
  Adder #(.width(1)) adder_3 (.a(in_13), .b(in_17), .out(out_29), .cin(adder_2_cout), .cout(adder_3_cout));
  Adder #(.width(1)) adder_4 (.a(in_12), .b(in_16), .out(out_28), .cin(adder_3_cout), .cout(out_27));
endmodule
